# Fritzing sketch roaster (saved by Fritzing 0.9.1b)
breadboards: 1

parts:
  4_Relay_Module1 = OPENMolo 4 Relay breakout board
  Bean_agitator_motor = DC Motor
  DC_motor_appropiate_adapter_power = LED Built-in Driver Power Supply
  Heating_element = Inductor [package="400 mil [THT]"]
  Halogen_oven_power_source = LED Built-in Driver Power Supply
  Bean_drop_electromagnet = Solenoid
  Electromagnet_power_source = LED Built-in Driver Power Supply
  Cooling_fan = Inductor [package="400 mil [THT]"]
  Cooling_fan_power_source = LED Built-in Driver Power Supply
  Part1 = Arduino Uno (Rev3) - ICSP
  Air_temp = MAX6675 [package=so08]
  Bean_temp = MAX6675 [package=so08]

nets:
  GND: 4_Relay_Module1.GND, Part1.GND, Air_temp.VSS, Bean_temp.VSS
  VDD: 4_Relay_Module1.VCC, Part1.5V, Air_temp.VDD, Bean_temp.VDD
  N1: 4_Relay_Module1.E4, Part1.D13/SCK
  N2: 4_Relay_Module1.E3, Part1.ICSP_MISO, Part1.D12/MISO
  N3: 4_Relay_Module1.E2, Part1.ICSP_MOSI, Part1.D11_PWM/MOSI
  N4: 4_Relay_Module1.E1, Part1.D10_PWM/SS
  N5: 4_Relay_Module1.PW_Rel_1, DC_motor_appropiate_adapter_power.VCC_IN#11
  N6: 4_Relay_Module1.NO_Rel_1, Bean_agitator_motor.pin_2
  N7: 4_Relay_Module1.PW_Rel_R2, Halogen_oven_power_source.VCC_IN#11
  N8: 4_Relay_Module1.NO_Rel_2, Heating_element.pin_1
  N9: 4_Relay_Module1.PW_Rel_3, Electromagnet_power_source.VCC_IN#11
  N10: 4_Relay_Module1.NO_Rel_3, Bean_drop_electromagnet.pin2
  N11: 4_Relay_Module1.NO_Rel_4, Cooling_fan.pin_1
  N12: Bean_agitator_motor.pin_1, DC_motor_appropiate_adapter_power.VCC_IN#10
  N13: Heating_element.pin_0, Halogen_oven_power_source.VCC_IN#10
  N14: Bean_drop_electromagnet.pin1, Electromagnet_power_source.VCC_IN#10
  N15: Cooling_fan.pin_0, Cooling_fan_power_source.VCC_IN#10
  N16: Part1.D2, Bean_temp.SCK
  N17: Part1.D3_PWM, Bean_temp.CS
  N18: Part1.D4, Bean_temp.MISO
  N19: Part1.D5_PWM, Air_temp.SCK
  N20: Part1.D6_PWM, Air_temp.CS
  N21: Part1.D7, Air_temp.MISO

custom parts:
  OPENMolo 4 Relay breakout board: Módulo de 8 relés de 10A optoaislados pensado para desarrollos rápidos basadon en microcontroladores o microcomputadoras. Estos módulos son diseñados con especial cuidado tanto en sus capacidades aisladoras para preservar equipos de mayor valor asi como en las fijaciones para evitar problemas a la hora de armar un prototipo o de fijarlo en un tablero definitivo. Una importante característica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
  LED Built-in Driver Power Supply: The power constant current constant voltage This circuit with overcurrent protection, short circuit, open circuit protection
